// Logisim project IT012_Lab01_25521107.circ as structural Verilog: 6 circuits, main circuit TN1
module Warmup (
  input  A,
  input  B,
  output F
);

  wire not_1_out;

  not not_1 (not_1_out, B);
  and and_1 (F, A, not_1_out);
endmodule

module TN1 (
  input  A,
  input  B,
  input  C,
  output A_prime,
  output AND,
  output OR,
  output NAND,
  output NOR,
  output XOR,
  output XNOR,
  output XOR3,
  output CHAIN,
  output NAND3
);

  wire nand_2_out;

  not not_1 (A_prime, A);
  and and_1 (AND, A, B);
  or or_1 (OR, A, B);
  nand nand_1 (NAND, A, B);
  nor nor_1 (NOR, A, B);
  xor xor_1 (XOR, A, B);
  xnor xnor_1 (XNOR, B, A);
  xor xor_2 (XOR3, A, B, C);
  nand nand_2 (nand_2_out, A, B);
  nand nand_3 (NAND3, A, B, C);
  nand nand_4 (CHAIN, nand_2_out, C);
endmodule

module TN2 (
  input  X,
  input  Y,
  input  Z,
  output EQ1,
  output EQ2,
  output EQ3,
  output EQ4,
  output EQ5
);

  wire and_1_out, and_2_out, and_3_out, and_4_out, nand_1_out, nor_1_out, not_1_out, not_2_out, or_1_out,
       or_2_out, or_3_out, or_4_out;

  not not_1 (not_1_out, X);
  nor nor_1 (nor_1_out, X, Y);
  not not_2 (not_2_out, Y);
  and and_1 (and_1_out, Y, Z);
  or or_1 (or_1_out, X, Y);
  or or_2 (or_2_out, X, Z);
  nand nand_1 (nand_1_out, X, Y);
  or or_3 (or_3_out, X, and_1_out);
  and and_2 (and_2_out, or_1_out, or_2_out);
  and and_3 (and_3_out, not_1_out, not_2_out);
  and and_4 (and_4_out, not_1_out, Y);
  or or_4 (or_4_out, and_4_out, X);
  xnor xnor_1 (EQ1, and_3_out, nor_1_out);
  xnor xnor_2 (EQ2, and_3_out, nand_1_out);
  xnor xnor_3 (EQ3, or_3_out, and_2_out);
  xnor xnor_4 (EQ4, or_4_out, X);
  xnor xnor_5 (EQ5, or_4_out, or_1_out);
endmodule

module TN3 (
  input  A,
  input  B,
  input  C,
  input  D,
  output F
);

  wire m2_out, m3_out, m5_out, m7_out, m11_out, m13_out, not_1_out, not_2_out, not_3_out, not_4_out;

  not not_1 (not_1_out, A);
  not not_2 (not_2_out, B);
  not not_3 (not_3_out, C);
  not not_4 (not_4_out, D);
  and m2 (m2_out, not_1_out, not_2_out, C, not_4_out);
  and m3 (m3_out, not_1_out, not_2_out, C, D);
  and m5 (m5_out, not_1_out, B, not_3_out, D);
  and m7 (m7_out, not_1_out, B, C, D);
  and m11 (m11_out, A, not_2_out, C, D);
  and m13 (m13_out, A, B, not_3_out, D);
  or or_1 (F, m2_out, m3_out, m5_out, m7_out, m11_out, m13_out);
endmodule

module TN4 (
  input  A,
  input  B,
  input  C,
  input  D,
  output F_can,
  output EQ1,
  output F_sop,
  output EQ2,
  output F_pos
);

  wire and_1_out, and_2_out, and_3_out, and_4_out, m2_out, m3_out, m5_out, m7_out, m11_out, m13_out,
       not_1_out, not_2_out, not_3_out, not_4_out, or_1_out, or_2_out, or_3_out, or_4_out;

  not not_1 (not_1_out, A);
  not not_2 (not_2_out, B);
  not not_3 (not_3_out, C);
  not not_4 (not_4_out, D);
  and m2 (m2_out, not_1_out, not_2_out, C, not_4_out);
  and m3 (m3_out, not_1_out, not_2_out, C, D);
  and m5 (m5_out, not_1_out, B, not_3_out, D);
  and m7 (m7_out, not_1_out, B, C, D);
  and m11 (m11_out, A, not_2_out, C, D);
  and m13 (m13_out, A, B, not_3_out, D);
  and and_1 (and_1_out, not_1_out, not_2_out, C);
  and and_2 (and_2_out, not_2_out, C, D);
  and and_3 (and_3_out, not_1_out, B, D);
  and and_4 (and_4_out, B, not_3_out, D);
  or or_1 (or_1_out, B, C);
  or or_2 (or_2_out, not_1_out, D);
  or or_3 (or_3_out, not_2_out, D);
  or or_4 (or_4_out, not_1_out, not_2_out, not_3_out);
  or or_5 (F_can, m2_out, m3_out, m5_out, m7_out, m11_out, m13_out);
  or or_6 (F_sop, and_1_out, and_2_out, and_3_out, and_4_out);
  and and_5 (F_pos, or_1_out, or_2_out, or_3_out, or_4_out);
  xnor xnor_1 (EQ1, F_can, F_sop);
  xnor xnor_2 (EQ2, F_can, F_pos);
endmodule

module TN5 (
  input  A,
  input  B,
  input  C,
  output F
);

  wire xor_1_out;

  xor xor_1 (xor_1_out, A, B);
  xor xor_2 (F, xor_1_out, C);
endmodule
